# Fritzing sketch clock-with-esp8266-and-ws2812-leds (saved by Fritzing 0.9.3b)

parts:
  U1 = ESP8266 NodeMCU LoLin module
  Part1 = Adafruit DS3231 [part_number="Adafruit #3013"]
  Part2 = KY-018 Photoresistor Module [package="Breakout board"]
  U2 = WS2812 RGB LED strip
  R1 = Resistor [tolerance=±5% resistance=220 package=THT]

nets:
  N1: U1.D1, Part1.SCL
  N2: U1.D2, Part1.SDA
  VIN: U1.3V3, Part1.Vin, Part2.Vin, U2.VCC
  GND: U1.GND, Part1.GND, Part2.-, U2.GND
  N3: U1.RX, R1.Pin_0
  N4: U1.A0, Part2.S
  N5: U2.DIN, R1.Pin_1

custom parts:
  ESP8266 NodeMCU LoLin module: ESP8266 based NodeMCU
  Adafruit DS3231: The datasheet for the DS3231 explains that this part is an "Extremely Accurate I²C-Integrated RTC/TCXO/Crystal". And, hey, it does exactly what it says on the tin! This Real Time Clock (RTC) is the most precise you can get in a small, low power package. Most RTCs use an external 32kHz timing crystal that is used to keep time with low current draw. And that's all well and good, but those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
  KY-018 Photoresistor Module: KY-018 Photoresistor module, used to measure light intensity. It can determine the presence or absence of light.
  WS2812 RGB LED strip: WS2812 strip
